# Fritzing sketch 328_term (saved by Fritzing 0.9.1b)
breadboards: 1

parts:
  JP1 = RCA [package=rca_lock]
  U1 = mini DIN 6 Connector [package=mini-din6]
  U2 = atmega328 [package=dip]
  U3 = atmega328 [package=dip]
  D1_1N4148 = Diode [package=diode-1n4148]
  D2_1N4148 = Diode [package=diode-1n4148]
  R4 = Resistor [tolerance=±5% resistance=1k package="1206 [SMD]"]
  R3 = Resistor [tolerance=±5% resistance=330 package="1206 [SMD]"]
  XTAL1 = Crystal [frequency="16 Mhz" package=THT]
  C8_-_22pf = Capacitor [package=cap-pth-small2]
  C7_-_22pf = Capacitor [package=cap-pth-small2]
  XTAL2 = Crystal [frequency="16 Mhz" package=THT]
  C5_-_22pf1 = Capacitor [package=cap-pth-small2]
  C6_-_22pf1 = Capacitor [package=cap-pth-small2]
  IC1 = Voltage Regulator [package=to220-igo]
  C4 = Ceramic Capacitor [capacitance=100nF package="100 mil [THT, multilayer]"]
  C3 = Ceramic Capacitor [capacitance=100nF package="100 mil [THT, multilayer]"]
  C1 = Ceramic Capacitor [capacitance=100nF package="100 mil [THT, multilayer]"]
  C2 = Ceramic Capacitor [capacitance=100nF package="100 mil [THT, multilayer]"]
  C10 = Capacitor Polarized [package=cpol-radial-10uf-25v]
  C9 = Capacitor Polarized [package=cpol-radial-10uf-25v]
  R1 = Resistor [tolerance=±5% resistance=10k package=THT]
  R2 = Resistor [tolerance=±5% resistance=10k package=THT]
  J1 = female pin header, 10 pins [form="♀ (female)"]
  J2 = female pin header, 10 pins [form="♀ (female)"]
  J3 = female pin header, 2 pins [form="♀ (female)"]

nets:
  N1: JP1.PIN, R4.Pin_1, R3.Pin_1
  GND: JP1.SHELL, U1.6, U2.GND, U3.GND#21, C8_-_22pf.2, C7_-_22pf.2, C5_-_22pf1.2, C6_-_22pf1.2, IC1.GND, C4.1, C1.0, C2.1, C10.-, C9.-, J2.pin3, J3.pin1
  5V: U1.3, U2.VCC, U2.AVCC, U3.VCC, U3.AVCC, IC1.OUT, C4.0, C3.1, C1.1, C2.0, R1.Pin_1, R2.Pin_1, J2.pin2
  N2: U1.4, U2.D3_(PWM)
  N3: U1.5, U2.D2
  N4: U2.RESET, R1.Pin_0
  N5: U2.D0_(RX), U3.D1_(TX)
  N6: U2.D1_(TX), U3.D0_(RX)
  D4: U2.D4, J1.pin10
  N7: U2.XLAT1, XTAL2.pin_1, C5_-_22pf1.1
  N8: U2.XLAT2, XTAL2.pin_0, C6_-_22pf1.1
  D5: U2.D5_(PWM), J1.pin9
  D6: U2.D6_(PWM), J1.pin8
  D7: U2.D7, J1.pin7
  D8: U2.D8, J1.pin6
  D9: U2.D9_(PWM), J1.pin5
  D10: U2.D10_(PWM), J1.pin4
  D11: U2.D11_(PWM), J1.pin3
  D12: U2.D12, J1.pin2
  D13: U2.D13, J1.pin1
  AREF: U2.AREF, J2.pin4
  A0: U2.A0, J2.pin10
  A1: U2.A1, J2.pin9
  A2: U2.A2, J2.pin8
  A3: U2.A3, J2.pin7
  A4: U2.A4, J2.pin6
  A5: U2.A5, J2.pin5
  N9: U3.RESET, R2.Pin_0
  N10: U3.GND#7, C3.0
  N11: U3.XLAT1, XTAL1.pin_1, C7_-_22pf.1
  N12: U3.XLAT2, XTAL1.pin_0, C8_-_22pf.1
  N13: U3.D9_(PWM), D1_1N4148.A
  N14: U3.D11_(PWM), D2_1N4148.A
  N15: D1_1N4148.C, R4.Pin_0
  N16: D2_1N4148.C, R3.Pin_0
  V IN: IC1.IN, C9.+, J2.pin1, J3.pin2

notes:
  sig_pixel
  sig_sync
  data
  clk
